// Logisim project control-logic.circ as structural Verilog: 1 circuit, main circuit control_logic
module control_logic (
  input  [31:0] Instruction,
  input  BrEq,
  input  BrLt,
  output PCSel,
  output RegWEn,
  output [2:0] ImmSel,
  output BrUn,
  output ASel,
  output BSel,
  output [3:0] ALUSel,
  output MemWEn,
  output [1:0] WBSel
);

  wire and_12_out, and_13_out, and_14_out, AUtype, bitselector_3_out, bitselector_4_out, bitselector_5_out,
       bitselector_6_out, bitselector_7_out, bitselector_8_out, bitselector_9_out, bitselector_10_out,
       bitselector_11_out, bitselector_12_out, Btype, fc3eq5, funct7_0, funct7_5, JItype, Jtype, Ltype,
       LUtype, not_1_out, not_2_out, not_3_out, not_4_out, not_5_out, not_6_out, not_7_out, not_8_out,
       not_9_out, not_10_out, not_11_out, not_12_out, not_13_out, not_14_out, not_15_out, not_16_out,
       not_17_out, not_18_out, not_19_out, not_20_out, not_21_out, not_22_out, not_23_out, not_24_out,
       not_25_out, not_26_out, not_27_out, not_28_out, not_29_out, not_30_out, not_31_out, not_32_out, Rtype,
       Stype;
  wire [1:0] priority_encoder_1_out;
  wire [3:0] priority_encoder_2_out, RtypeRes;
  wire [3:3] ItypeRes;

  BitSelector #(.width(7)) bitselector_1 (.in(Instruction[31:25]), .out(funct7_0), .sel(3'b000));
  BitSelector #(.width(7)) bitselector_2 (.in(Instruction[31:25]), .out(funct7_5), .sel(3'b101));
  // Probe on bitselector_3_out
  BitSelector #(.width(7)) bitselector_3 (.in(Instruction[6:0]), .out(bitselector_3_out), .sel(3'b000));
  // Probe on bitselector_4_out
  BitSelector #(.width(7)) bitselector_4 (.in(Instruction[6:0]), .out(bitselector_4_out), .sel(3'b001));
  // Probe on bitselector_5_out
  BitSelector #(.width(7)) bitselector_5 (.in(Instruction[6:0]), .out(bitselector_5_out), .sel(3'b010));
  // Probe on bitselector_6_out
  BitSelector #(.width(7)) bitselector_6 (.in(Instruction[6:0]), .out(bitselector_6_out), .sel(3'b011));
  // Probe on bitselector_7_out
  BitSelector #(.width(7)) bitselector_7 (.in(Instruction[6:0]), .out(bitselector_7_out), .sel(3'b100));
  // Probe on bitselector_8_out
  BitSelector #(.width(7)) bitselector_8 (.in(Instruction[6:0]), .out(bitselector_8_out), .sel(3'b101));
  // Probe on bitselector_9_out
  BitSelector #(.width(7)) bitselector_9 (.in(Instruction[6:0]), .out(bitselector_9_out), .sel(3'b110));
  not not_1 (not_1_out, bitselector_5_out);
  not not_2 (not_2_out, bitselector_6_out);
  not not_3 (not_3_out, bitselector_8_out);
  not not_4 (not_4_out, bitselector_9_out);
  not not_5 (not_5_out, bitselector_5_out);
  not not_6 (not_6_out, bitselector_6_out);
  not not_7 (not_7_out, bitselector_9_out);
  not not_8 (not_8_out, bitselector_5_out);
  not not_9 (not_9_out, bitselector_6_out);
  not not_10 (not_10_out, bitselector_7_out);
  not not_11 (not_11_out, bitselector_5_out);
  not not_12 (not_12_out, bitselector_6_out);
  not not_13 (not_13_out, bitselector_7_out);
  not not_14 (not_14_out, bitselector_8_out);
  not not_15 (not_15_out, bitselector_9_out);
  not not_16 (not_16_out, bitselector_5_out);
  not not_17 (not_17_out, bitselector_6_out);
  not not_18 (not_18_out, bitselector_7_out);
  not not_19 (not_19_out, bitselector_9_out);
  not not_20 (not_20_out, bitselector_7_out);
  not not_21 (not_21_out, bitselector_6_out);
  not not_22 (not_22_out, bitselector_7_out);
  not not_23 (not_23_out, bitselector_6_out);
  not not_24 (not_24_out, bitselector_8_out);
  not not_25 (not_25_out, bitselector_9_out);
  not not_26 (not_26_out, bitselector_6_out);
  not not_27 (not_27_out, bitselector_9_out);
  and and_1 (BSel, bitselector_3_out, bitselector_4_out, not_1_out, not_2_out, bitselector_7_out, not_3_out, not_4_out);
  and and_2 (Rtype, bitselector_3_out, bitselector_4_out, not_5_out, not_6_out, bitselector_7_out, bitselector_8_out, not_7_out);
  and and_3 (Btype, bitselector_3_out, bitselector_4_out, not_8_out, not_9_out, not_10_out, bitselector_8_out, bitselector_9_out);
  and and_4 (Ltype, bitselector_3_out, bitselector_4_out, not_11_out, not_12_out, not_13_out, not_14_out, not_15_out);
  and and_5 (Stype, bitselector_3_out, bitselector_4_out, not_16_out, not_17_out, not_18_out, bitselector_8_out, not_19_out);
  and and_6 (Jtype, bitselector_3_out, bitselector_4_out, bitselector_5_out, bitselector_6_out, not_20_out, bitselector_8_out, bitselector_9_out);
  and and_7 (JItype, bitselector_3_out, bitselector_4_out, bitselector_5_out, not_21_out, not_22_out, bitselector_8_out, bitselector_9_out);
  and and_8 (AUtype, bitselector_3_out, bitselector_4_out, bitselector_5_out, not_23_out, bitselector_7_out, not_24_out, not_25_out);
  and and_9 (LUtype, bitselector_3_out, bitselector_4_out, bitselector_5_out, not_26_out, bitselector_7_out, bitselector_8_out, not_27_out);
  BitSelector #(.width(3)) bitselector_10 (.in(Instruction[14:12]), .out(bitselector_10_out), .sel(2'b00));
  BitSelector #(.width(3)) bitselector_11 (.in(Instruction[14:12]), .out(bitselector_11_out), .sel(2'b01));
  BitSelector #(.width(3)) bitselector_12 (.in(Instruction[14:12]), .out(bitselector_12_out), .sel(2'b10));
  and and_10 (ItypeRes[3], fc3eq5, funct7_5);
  not not_28 (not_28_out, funct7_0);
  not not_29 (not_29_out, funct7_5);
  not not_30 (not_30_out, funct7_5);
  not not_31 (not_31_out, funct7_0);
  not not_32 (not_32_out, bitselector_11_out);
  and and_11 (fc3eq5, bitselector_10_out, not_32_out, bitselector_12_out);
  and and_12 (and_12_out, not_28_out, not_29_out);
  and and_13 (and_13_out, funct7_0, not_30_out);
  and and_14 (and_14_out, not_31_out, funct7_5);
  Priority_Encoder #(.select_enc(2)) priority_encoder_1 (
    .in0(and_12_out), .in2(and_13_out), .in3(and_14_out), .out(priority_encoder_1_out));  // open: in1, gs, en_out, en_in
  // Probe on {priority_encoder_1_out, 2'b00}
  assign RtypeRes = {1'b0, Instruction[14:12]} | {priority_encoder_1_out, 2'b00};  // OR_Gate or_1, 4 bits wide
  // Probe on RtypeRes
  Priority_Encoder #(.select_enc(4)) priority_encoder_2 (
    .in0(BSel), .in1(Rtype), .out(priority_encoder_2_out));  // open: in2, in3, in4, in5, in6, in7, in8, in9, in10, in11, in12, in13, in14, in15, gs, en_out, en_in
  Multiplexer #(.select(4), .width(4)) multiplexer_1 (
    .in0({ItypeRes[3], Instruction[14:12]}), .in1(RtypeRes), .out(ALUSel), .sel(priority_encoder_2_out));  // open: in2, in3, in4, in5, in6, in7, in8, in9, in10, in11, in12, in13, in14, in15

  assign RegWEn = 1'b1;

  // Other names for the same wires on the sheet: funct3[2:0] = Instruction[14:12]; ItypeRes[2:0] = Instruction[14:12];
  //   Itype = BSel

  // Notes on the sheet:
  //   INPUTS to your circuit
  //   DON'T CHANGE THE LOCATIONS OF THE INPUTS AND OUTPUTS!
  //   OUTPUT from your circuit
endmodule
