// Logisim project imm-gen.circ as structural Verilog: 1 circuit, main circuit imm_gen
module imm_gen (
  input  [31:0] Instruction,
  input  [2:0] ImmSel,
  output [31:0] Immediate
);

  // Probe on Instruction[31]
  // Probe on Instruction[30:20]
  Multiplexer #(.width(21)) multiplexer_1 (
    .in0({21{1'b0}}), .in1({21{1'b1}}), .out(Immediate[31:11]), .sel(Instruction[31]));
  // Probe on {Immediate[31:11], Instruction[30:20]}

  assign Immediate[10:0] = Instruction[30:20];

  // Other names for the same wires on the sheet: imm_11_0[11:0] = Instruction[31:20]; opcode[6:0] = Instruction[6:0];
  //   rd[4:0] = Instruction[11:7]; funct3[2:0] = Instruction[14:12]; rs1[4:0] = Instruction[19:15]

  // Notes on the sheet:
  //   INPUTS to your circuit
  //   DON'T CHANGE THE LOCATIONS OF THE INPUTS AND OUTPUTS!
  //   OUTPUT from your circuit
endmodule
